# Fritzing sketch compressor (saved by Fritzing 1.0.5)
circuit board: 20cm x 20cm
breadboards: 1

parts:
  DC-DC_WAVGAT_mini560_9V = mini560 [package=THT]
  Реле = 2-Channel 5v Relay Shield [package=relay-2ch5v10a]
  Arduino_UNO_R3 = Arduino Uno (Rev3)
  DC-DC_WAVGAT_mini560_5V = mini560 [package=THT]
  R1 = Resistor [tolerance=±5% power=0.25W resistance=1k package=THT]
  Мосфет = IFR520 MOS module [package=THT]
  Реле_отключения_сигнала_HK19F = Mini Power Relay-HK19F [package=HK19F]
  Компонент1 = Arduino Nano (Rev3.0)  # not connected

nets:
  GND: DC-DC_WAVGAT_mini560_9V.pin_6, DC-DC_WAVGAT_mini560_9V.pin_7, Реле.GND, Arduino_UNO_R3.GND, DC-DC_WAVGAT_mini560_5V.pin_3, DC-DC_WAVGAT_mini560_5V.pin_6, DC-DC_WAVGAT_mini560_5V.pin_7, Мосфет.pin3, Реле_отключения_сигнала_HK19F.COIL#15
  N1: DC-DC_WAVGAT_mini560_9V.pin_8, DC-DC_WAVGAT_mini560_9V.pin_9, Arduino_UNO_R3.VIN
  VCC: Реле.VCC, Arduino_UNO_R3.5V, R1.Pin_1, Мосфет.pin2
  N2: Реле.IN1, Arduino_UNO_R3.D7
  N3: Реле.IN2, Arduino_UNO_R3.D4
  N4: Реле.JD-VCC, Arduino_UNO_R3.D2, DC-DC_WAVGAT_mini560_5V.pin_8, DC-DC_WAVGAT_mini560_5V.pin_9, Реле_отключения_сигнала_HK19F.COIL#0
  N5: Arduino_UNO_R3.A0, Реле_отключения_сигнала_HK19F.NO_A
  N6: Arduino_UNO_R3.A3, Реле_отключения_сигнала_HK19F.NO_B
  N7: Arduino_UNO_R3.A4/SDA, R1.Pin_0
  N8: Arduino_UNO_R3.D9_PWM, Мосфет.pin1
  ДАД+ДТВ 2 на впускном коллекторе, OUT, ДАД/ДПДЗ, OUT, выход C/Заслонка ВАЗ 21126, ток 180мА, +/Заслонка ВАЗ 21126, ток 180мА, -/Коннектор, у ЭБУ/Коннектор, у блока управления/Сине-жёлый, стандартная проводка/Точка соединения со стандартной проводкой рядом с ДПДЗ/Точка соединения, в блоке управления/ЭБУ, Январь 5.1, pin 40: Arduino_UNO_R3.D3_PWM, Реле_отключения_сигнала_HK19F.COM_A, Реле_отключения_сигнала_HK19F.COM_B

notes:
  +, 0,35
  -, 0,35
  out, 0,35
  out, розово-зелёный, 0,5
  out, голубо-оранжевый с жёлтой меткой, 0,75
  in, 0,35
  -, сине-зелёный, 1,5
  +, сине-красный, 1,0
  out, розово-зелёный с красной меткой, 0,5

custom parts:
  mini560: 5A DC-DC Mini 560 Step Down Stabilized Voltage Supply Module Output 3.3 5V 9V 12V Step-down Power Converter Board Module
  2-Channel 5v Relay Shield: 2 Channel 5v Relay Shield w. 2x SPD-06VDC-SD-C
  Mini Power Relay-HK19F: DC 3V, 5V, 6V, 9V, 12V, and, 24V Coil DPDT 8 Pin 2NO 2NC Mini Power Relays PCB Type HK19F
